# Fritzing sketch Breakout Board Smart Keychain (saved by Fritzing 0.8.7b)
# ESP32 breakout COMPACT license: CC-BY SA 4.0
breadboards: 1

parts:
  U1 = ESP32 breakout COMPACT
  S1 = Pushbutton [package="[THT]"]
  S2 = Pushbutton [package="[THT]"]
  S3 = Pushbutton [package="[THT]"]
  S4 = Pushbutton [package="[THT]"]
  R1 = Resistor [tolerance=±5% resistance=1k package=THT]
  R2 = Resistor [tolerance=±5% resistance=1k package=THT]
  R3 = Resistor [tolerance=±5% resistance=1k package=THT]
  R4 = Resistor [tolerance=±5% resistance=1k package=THT]
  LED1 = LED - 5mm [color="Red (633nm)" package="5 mm [THT]"]
  R5 = Resistor [tolerance=±5% resistance=1k package=THT]
  Part3 = Triple Axis Accelerometer Breakout - ADXL345
  V1 = DC Power [voltage=3.3V]

nets:
  N1: U1.D32, Part3.BUSY
  N2: U1.D33, R5.Pin_1
  N3: U1.D26, S1.Pin_1, S1.Pin_2, R1.Pin_0
  N4: U1.D27, Part3.DC
  N5: U1.D14, S3.Pin_1, S3.Pin_2, R3.Pin_0
  N6: U1.D13, S2.Pin_1, S2.Pin_2, R2.Pin_0
  N7: U1.GND, R1.Pin_1, R2.Pin_1, R3.Pin_1, R4.Pin_1, LED1.cathode
  VIN: U1.Vin, S1.Pin_4, S2.Pin_3, S2.Pin_4, S3.Pin_3, S3.Pin_4, S4.Pin_3, S4.Pin_4, Part3.VCC, V1.V+
  N8: U1.D2, S4.Pin_1, S4.Pin_2, R4.Pin_0
  N9: U1.D5, Part3.DIN
  N10: U1.D18, Part3.CLK
  N11: U1.D19, Part3.CS
  N12: U1.D23, Part3.RST
  N13: LED1.anode, R5.Pin_0
  N14: Part3.GND, V1.V-

notes:
  E- Paper Display

custom parts:
  ESP32 breakout COMPACT: ESP-WROOM-32 ピッチ変換基板 コンパクト by a bit better circuit ES2-WROON-32 breakout board COMPACT ESP32-WROOM-32 Image from DOIT Esp32 DevKit v1 (30 pins long, 11 pins width) by Werner Rothschopf (modified by vanepp Dec 2018)
  Triple Axis Accelerometer Breakout - ADXL345: Description: This new version adds 2 standoff holes as well as an extra decoupling capacitor. The ADXL345 is a small, thin, low power, 3-axis accelerometer with high resolution (13-bit) measurement at up to ±16 g. Digital output data is formatted as 16-bit twos complement and is accessible through either a SPI (3- or 4-wire) or I2C digital interface. The ADXL345 is well suited to measures the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
