# Fritzing sketch SMART KEYCHAIN (saved by Fritzing 0.8.7b)
breadboards: 1

parts:
  M1 = DOIT Esp32 DevKit v1 (30 pins long, 11 pins width) [part_number=ESP32S-PIN30]
  S1 = Pushbutton [package="[THT]"]
  S2 = Pushbutton [package="[THT]"]
  S3 = Pushbutton [package="[THT]"]
  S4 = Pushbutton [package="[THT]"]
  R2 = Resistor [tolerance=±5% resistance=1k package=THT]
  R3 = Resistor [tolerance=±5% resistance=1k package=THT]
  R4 = Resistor [tolerance=±5% resistance=1k package=THT]
  R1 = Resistor [tolerance=±5% resistance=1k package=THT]
  V1 = DC Power [voltage=5]
  Part2 = Triple Axis Accelerometer Breakout - ADXL345
  R5 = Resistor [tolerance=±5% resistance=220 package=THT]
  LED1 = LED - 5mm [color="Red (633nm)" package="5 mm [THT]"]

nets:
  N1: M1.3V3, S1.Pin_4, S2.Pin_4, S3.Pin_4, S4.Pin_3, S4.Pin_4
  GND: M1.GND, R2.Pin_1, R3.Pin_1, R4.Pin_1, R1.Pin_1, V1.V-, Part2.GND, LED1.cathode
  N2: M1.D2, S4.Pin_1, S4.Pin_2, R4.Pin_0
  N3: M1.D4, Part2.DIN
  N4: M1.D18, Part2.CLK
  N5: M1.D23, Part2.RST
  N6: M1.D34, Part2.CS
  N7: M1.D32, Part2.BUSY
  N8: M1.D33, R5.Pin_1
  N9: M1.D26, S1.Pin_1, S1.Pin_2, R1.Pin_0
  N10: M1.D27, Part2.DC
  N11: M1.D14, S3.Pin_1, S3.Pin_2, R3.Pin_0
  N12: M1.D13, S2.Pin_1, S2.Pin_2, R2.Pin_0
  VIN: M1.VIN, V1.V+, Part2.VCC
  N13: R5.Pin_0, LED1.anode

notes:
  E- Paper Display

custom parts:
  DOIT Esp32 DevKit v1 (30 pins long, 11 pins width): The DOIT Esp32 DevKit v1 is one of the development board created by DOIT to evaluate the ESP-WROOM-32 module. It is based on the ESP32 microcontroller that boasts Wifi, Bluetooth, Ethernet and Low Power support all in a single chip. (vanepp) made breadboard work, adjusted pin numbering and labels and reduced size of schematic and cleaned up pcb. This chip is 30pins long (2 x15) and 11 pins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
  Triple Axis Accelerometer Breakout - ADXL345: Description: This new version adds 2 standoff holes as well as an extra decoupling capacitor. The ADXL345 is a small, thin, low power, 3-axis accelerometer with high resolution (13-bit) measurement at up to ±16 g. Digital output data is formatted as 16-bit twos complement and is accessible through either a SPI (3- or 4-wire) or I2C digital interface. The ADXL345 is well suited to measures the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
